# Fritzing sketch ColorSensor (saved by Fritzing 0.9.3b)
breadboards: 1

parts:
  Part1 = Arduino Uno (Rev3)
  BT1 = Bluetooth HC-06u [package=THT]
  LED1 = RGB LED (com. cathode, rgb) [package="5 mm [THT]"]
  R1 = Photocell (LDR) [package=THT]
  R2 = Resistor [tolerance=±5% resistance=220 package=THT]

nets:
  N1: Part1.A0, R1.pin_0, R2.Pin_1
  N2: Part1.D11_PWM/MOSI, LED1.red_anode
  N3: Part1.D12/MISO, LED1.green_anode
  N4: Part1.D13/SCK, LED1.blue_anode
  N5: Part1.D0/RX, BT1.TXD
  N6: Part1.D1/TX, BT1.RXD
  5V: Part1.5V, BT1.VCC, R2.Pin_0
  GND: Part1.GND, BT1.GND, LED1.common_cathode, R1.pin_1

custom parts:
  Bluetooth HC-06u: Bluetooth HC-06 - face up, pins down 16.5mm x 37.5mm PCB
